# Fritzing sketch diagram (saved by Fritzing 0.9.4)
perfboards: 1

parts:
  Part1 = Arduino Mega 2560 (Rev3)
  Raspberry_Pi_1 = Raspberry Pi 3 [part_number=RPI-3-V1.2]  # not connected
  Ice_Motor = Stepper Motor - Bipolar
  Tray_Motor = Stepper Motor - Bipolar
  Pololu_A1 = Pololu A4988 [package=SO16]
  Pololu_A2 = Pololu A4988 [package=SO16]
  Pump_1 = DC Motor
  Pump_2 = DC Motor
  Pump_3 = DC Motor
  V1 = DC Power [voltage=5V]  # not connected
  V2 = DC Power [voltage=12V]
  C2 = Capacitor Polarized [package=cpol-radial-100uf-25v]
  C3 = Capacitor Polarized [package=cpol-radial-100uf-25v]
  U1 = L298_BRIDGE_DRIVER [package=powerso20]
  Pump_4 = DC Motor
  U2 = L298_BRIDGE_DRIVER [package=powerso20]

nets:
  N1: Part1.D11_PWM, U2.ENA
  N2: Part1.D10_PWM, U2.ENB
  N3: Part1.D8_PWM, U1.ENB
  N4: Part1.D2_PWM, Pololu_A1.DIR
  N5: Part1.D3_PWM, Pololu_A1.STEP
  N6: Part1.D4_PWM, Pololu_A2.DIR
  N7: Part1.D5_PWM, Pololu_A2.STEP
  N8: Part1.D7_PWM, U1.ENA
  VDD: Part1.5V, Pololu_A1.VDD, Pololu_A2.VDD
  N9: Part1.D27, U1.IN1
  N10: Part1.D28, U1.IN2
  N11: Part1.D29, U1.IN3
  N12: Part1.D30, U1.IN4
  N13: Part1.D31, U2.IN1
  N14: Part1.D32, U2.IN2
  N15: Part1.D33, U2.IN4
  N16: Part1.D34, U2.IN3
  GND: Part1.GND, Pololu_A1.GND, Pololu_A2.GND, C2.-, C3.-, U1.GND, U2.GND
  N17: Ice_Motor.A, Pololu_A1.1A
  N18: Ice_Motor.C, Pololu_A1.1B
  N19: Ice_Motor.B, Pololu_A1.2A
  N20: Ice_Motor.D, Pololu_A1.2B
  N21: Tray_Motor.A, Pololu_A2.1A
  N22: Tray_Motor.C, Pololu_A2.1B
  N23: Tray_Motor.B, Pololu_A2.2A
  N24: Tray_Motor.D, Pololu_A2.2B
  N25: Pololu_A1.RESET, Pololu_A1.SLEEP
  VSS: Pololu_A1.VMOT, Pololu_A2.VMOT, V2.V+, C2.+, C3.+, U1.VSS, U2.VSS
  N26: Pololu_A2.RESET, Pololu_A2.SLEEP
  N27: Pump_1.pin_1, U1.OUT1
  N28: Pump_1.pin_2, U1.OUT2
  N29: Pump_2.pin_1, U1.OUT4
  N30: Pump_2.pin_2, U1.OUT3
  N31: Pump_3.pin_1, U2.OUT1
  N32: Pump_3.pin_2, U2.OUT2
  N33: Pump_4.pin_1, U2.OUT4
  N34: Pump_4.pin_2, U2.OUT3
